# Fritzing sketch Sistema completo (saved by Fritzing 0.9.3b)
breadboards: 4

parts:
  MH-ET_LIVE_ESP32_DEVKIT2 = MH-ET LIVE ESP32 DEVKIT 38 pins
  R7 = Resistor [tolerance=±5% resistance=220 package=THT]
  R8 = Resistor [tolerance=±5% resistance=220 package=THT]
  R9 = Resistor [tolerance=±5% resistance=220 package=THT]
  R10 = Resistor [tolerance=±5% resistance=220 package=THT]
  R11 = Resistor [tolerance=±5% resistance=220 package=THT]
  LED6 = LED - 5mm [color="Red (633nm)" package="5 mm [THT]"]
  LED7 = LED - 5mm [color="Red (633nm)" package="5 mm [THT]"]
  LED8 = LED - 5mm [color="Red (633nm)" package="5 mm [THT]"]
  LED9 = LED - 5mm [color="Red (633nm)" package="5 mm [THT]"]
  LED10 = LED - 5mm [color="Red (633nm)" package="5 mm [THT]"]
  J2 = Piezo Speaker
  S2 = Pushbutton [package="[SMD]"]
  R12 = Resistor [tolerance=±5% resistance=220 package=THT]
  J3 = Basic Servo
  Componente2 = RFID-RC522-v2
  LED11 = LED - 5mm [color="Green (555nm)" package="5 mm [THT]"]
  R13 = Resistor [tolerance=±5% resistance=220 package=THT]
  R14 = Resistor [tolerance=±5% resistance=220 package=THT]
  LED12 = LED - 5mm [color="Red (633nm)" package="5 mm [THT]"]
  Part1 = KY-037 High Sensitivity Sound Detection Module [package="Breakout board"]
  RHT1 = Humidity and Temperature Sensor RHT03
  hc-sr1 = hc-sr04
  R15 = Photocell (LDR) [package=THT]
  R16 = Resistor [tolerance=±5% resistance=220 package=THT]

nets:
  3V3: MH-ET_LIVE_ESP32_DEVKIT2.3V3, RHT1.Vcc
  N1: MH-ET_LIVE_ESP32_DEVKIT2.IO35, Part1.D0
  N2: MH-ET_LIVE_ESP32_DEVKIT2.IO33, S2.Pin_1, S2.Pin_2, R12.Pin_0
  N3: MH-ET_LIVE_ESP32_DEVKIT2.IO25, hc-sr1.Trig
  N4: MH-ET_LIVE_ESP32_DEVKIT2.IO26, hc-sr1.Echo
  N5: MH-ET_LIVE_ESP32_DEVKIT2.IO27, R11.Pin_1
  N6: MH-ET_LIVE_ESP32_DEVKIT2.IO14, R9.Pin_1
  N7: MH-ET_LIVE_ESP32_DEVKIT2.IO12, R15.pin_1, R16.Pin_0
  N8: MH-ET_LIVE_ESP32_DEVKIT2.IO13, J3.pulse
  N9: MH-ET_LIVE_ESP32_DEVKIT2.SD3, RHT1.Data-signal
  VCC: MH-ET_LIVE_ESP32_DEVKIT2.5V, S2.Pin_3, S2.Pin_4, J3.vcc, Componente2.3.3V, Part1.+, hc-sr1.VCC, R15.pin_0
  GND: MH-ET_LIVE_ESP32_DEVKIT2.GND#64, LED6.cathode, LED7.cathode, LED8.cathode, LED9.cathode, LED10.cathode, J2.pin1, R12.Pin_1, J3.gnd, Componente2.GND
  N10: MH-ET_LIVE_ESP32_DEVKIT2.IO23, Componente2.MOSI
  N11: MH-ET_LIVE_ESP32_DEVKIT2.IO21, R14.Pin_1
  N12: MH-ET_LIVE_ESP32_DEVKIT2.GND#70, LED11.cathode, LED12.cathode, RHT1.GND_2, R16.Pin_1
  N13: MH-ET_LIVE_ESP32_DEVKIT2.IO19, Componente2.MISO
  N14: MH-ET_LIVE_ESP32_DEVKIT2.IO18, Componente2.SCK
  N15: MH-ET_LIVE_ESP32_DEVKIT2.IO5, R13.Pin_1
  N16: MH-ET_LIVE_ESP32_DEVKIT2.IO17, Componente2.SDA
  N17: MH-ET_LIVE_ESP32_DEVKIT2.IO16, R8.Pin_1
  N18: MH-ET_LIVE_ESP32_DEVKIT2.IO4, Componente2.RST
  N19: MH-ET_LIVE_ESP32_DEVKIT2.IO0, R7.Pin_1
  N20: MH-ET_LIVE_ESP32_DEVKIT2.IO2, R10.Pin_1
  N21: MH-ET_LIVE_ESP32_DEVKIT2.IO15, J2.pin2
  N22: R7.Pin_0, LED6.anode
  N23: R8.Pin_0, LED7.anode
  N24: R9.Pin_0, LED9.anode
  N25: R10.Pin_0, LED10.anode
  N26: R11.Pin_0, LED8.anode
  N27: LED11.anode, R14.Pin_0
  N28: R13.Pin_0, LED12.anode
  N29: Part1.A0, Part1.G, hc-sr1.GND

custom parts:
  MH-ET LIVE ESP32 DEVKIT 38 pins: http://mh.nodebb.com/topic/2/mh-et-live-esp32-devkit
  RFID-RC522-v2: A simple China made RFID-RC522 Reader; do check the pin labels, as this is a MFRC522 based clone.
  KY-037 High Sensitivity Sound Detection Module: KY-037 high sensitivity sound detection module is an analog/digital sensor that uses a condenser microphone to observe changes in environment noise.
